# Fritzing sketch 10ledswitch_rasp (saved by Fritzing 0.9.3b)
breadboards: 1

parts:
  Raspberry_Pi_2 = Raspberry Pi 3 [part_number=RPI-3-V1.2]
  LED11 = LED - 5mm [color="Red (633nm)" package="5 mm [THT]"]
  LED12 = LED - 5mm [color="Red (633nm)" package="5 mm [THT]"]
  LED13 = LED - 5mm [color="Red (633nm)" package="5 mm [THT]"]
  LED14 = LED - 5mm [color="Red (633nm)" package="5 mm [THT]"]
  LED15 = LED - 5mm [color="Red (633nm)" package="5 mm [THT]"]
  LED16 = LED - 5mm [color="Red (633nm)" package="5 mm [THT]"]
  LED17 = LED - 5mm [color="Red (633nm)" package="5 mm [THT]"]
  LED18 = LED - 5mm [color="Red (633nm)" package="5 mm [THT]"]
  LED19 = LED - 5mm [color="Red (633nm)" package="5 mm [THT]"]
  LED20 = LED - 5mm [color="Red (633nm)" package="5 mm [THT]"]
  S1 = Pushbutton [package="[THT]"]

nets:
  N1: Raspberry_Pi_2.GIPO4, LED15.anode
  N2: Raspberry_Pi_2.GND, Raspberry_Pi_2.GIPO19, LED11.cathode, LED12.cathode, LED13.cathode, LED13.anode, LED14.cathode, LED15.cathode, LED16.cathode, LED17.cathode, LED18.cathode, LED19.cathode, LED20.cathode
  N3: Raspberry_Pi_2.GIPO17, LED16.anode
  N4: Raspberry_Pi_2.GIPO27, LED19.anode
  N5: Raspberry_Pi_2.GIPO22, LED20.anode
  N6: Raspberry_Pi_2.GIPO6, LED14.anode
  N7: Raspberry_Pi_2.GIPO13, LED18.anode
  N8: Raspberry_Pi_2.GIPO24, LED17.anode
  N9: Raspberry_Pi_2.GIPO23, S1.Pin_4
  N10: Raspberry_Pi_2.GIPO18, LED11.anode
  N11: Raspberry_Pi_2.5V, S1.Pin_2
