# Fritzing sketch led (saved by Fritzing 0.9.3b)
breadboards: 1

parts:
  부품1 = Arduino Uno (Rev3)
  R1 = Resistor [tolerance=±5% resistance=220 package=THT]
  LED1 = LED - 5mm [color="Red (633nm)" package="5 mm [THT]"]

nets:
  N1: 부품1.D11_PWM/MOSI, LED1.anode
  N2: 부품1.GND, R1.Pin_0
  N3: R1.Pin_1, LED1.cathode
