# Fritzing sketch led_rasp (saved by Fritzing 0.9.3b)
breadboards: 1

parts:
  Raspberry_Pi_1 = Raspberry Pi 3 [part_number=RPI-3-V1.2]
  LED1 = smd LED [color="Red (633nm)" package="1206 [SMD]"]
  R1 = Resistor [tolerance=±5% resistance=220 package=THT]

nets:
  N1: Raspberry_Pi_1.GIPO17, R1.Pin_1
  N2: Raspberry_Pi_1.5V, LED1.cathode
  N3: LED1.anode, R1.Pin_0
