# Fritzing sketch line_follower (saved by Fritzing 0.9.3b)
breadboards: 1

parts:
  M1 = DC Motor
  M2 = DC Motor
  부품1 = Arduino Uno (Rev3)
  IC1 = L293D [package=THT]
  J3 = Infrared Proximity Sensor
  J4 = Infrared Proximity Sensor
  J5 = Infrared Proximity Sensor
  J1 = Infrared Proximity Sensor
  J2 = Infrared Proximity Sensor

nets:
  N1: M1.pin_1, IC1.Out_4_(_Controlled_by_Enable_2_)
  N2: M1.pin_2, IC1.Out_3_(_Controlled_by_Enable_2_)
  N3: M2.pin_1, IC1.Out_1_(_Controlled_by_Enable_1_)
  N4: M2.pin_2, IC1.Out_2_(_Controlled_by_Enable_1_)
  N5: 부품1.D8, IC1.In_2
  N6: 부품1.D9_PWM, IC1.In_1
  N7: 부품1.D10_PWM/SS, IC1.Enable_2
  N8: 부품1.D11_PWM/MOSI, IC1.Enable_1
  N9: 부품1.D12/MISO, IC1.In_4
  N10: 부품1.D2, J5.Vout
  N11: 부품1.D3_PWM, J4.Vout
  N12: 부품1.D4, J3.Vout
  N13: 부품1.D5_PWM, J2.Vout
  N14: 부품1.D6_PWM, J1.Vout
  N15: 부품1.D7, IC1.In_3
  GND: 부품1.GND, IC1.0V, J3.GND, J4.GND, J5.GND, J1.GND, J2.GND
  VCC: 부품1.VIN, IC1.+Vmotor, IC1.+V, J3.Vcc, J4.Vcc, J5.Vcc, J1.Vcc, J2.Vcc
