# Fritzing sketch self_balancing_robot (saved by Fritzing 0.9.3b)
breadboards: 1

parts:
  S1 = H-Bridge with L298N
  M1 = DC Motor
  M2 = DC Motor
  부품1 = Arduino Uno (Rev3)
  GY1 = MPU-6050 Board GY-521 [form="♀ (female)" package=THT]

nets:
  12V: S1.12V, 부품1.VIN
  GND: S1.GND, 부품1.GND, GY1.pin2
  N1: S1.ENA, 부품1.D11_PWM/MOSI
  N2: S1.IN1, 부품1.D9_PWM
  N3: S1.IN2, 부품1.D8
  N4: S1.IN3, 부품1.D12/MISO
  N5: S1.IN4, 부품1.D6_PWM
  N6: S1.ENB, 부품1.D10_PWM/SS
  N7: S1.M1-01, M2.pin_2
  N8: S1.M1-02, M2.pin_1
  N9: S1.M2-01, M1.pin_2
  N10: S1.M2-02, M1.pin_1
  N11: 부품1.A4/SDA, GY1.pin4
  N12: 부품1.D2, GY1.pin8
  N13: 부품1.3V3, GY1.pin1

custom parts:
  H-Bridge with L298N: h-bridge
  MPU-6050 Board GY-521: Acelerometro y Giroscopio MPU-6050 Board GY-521
