# Fritzing sketch ultrasonic (saved by Fritzing 0.9.3b)

parts:
  부품1 = Arduino Uno (Rev3)
  hc-sr1 = hc-sr04

nets:
  N1: 부품1.D6_PWM, hc-sr1.Echo
  N2: 부품1.D7, hc-sr1.Trig
  5V: 부품1.5V, hc-sr1.VCC
  GND: 부품1.GND, hc-sr1.GND
