# Fritzing sketch 10led_rasp (saved by Fritzing 0.9.3b)
breadboards: 1

parts:
  Raspberry_Pi_1 = Raspberry Pi 3 [part_number=RPI-3-V1.2]
  LED1 = LED - 5mm [color="Red (633nm)" package="5 mm [THT]"]
  LED2 = LED - 5mm [color="Red (633nm)" package="5 mm [THT]"]
  LED3 = LED - 5mm [color="Red (633nm)" package="5 mm [THT]"]
  LED4 = LED - 5mm [color="Red (633nm)" package="5 mm [THT]"]
  LED5 = LED - 5mm [color="Red (633nm)" package="5 mm [THT]"]
  LED6 = LED - 5mm [color="Red (633nm)" package="5 mm [THT]"]
  LED7 = LED - 5mm [color="Red (633nm)" package="5 mm [THT]"]
  LED8 = LED - 5mm [color="Red (633nm)" package="5 mm [THT]"]
  LED9 = LED - 5mm [color="Red (633nm)" package="5 mm [THT]"]
  LED10 = LED - 5mm [color="Red (633nm)" package="5 mm [THT]"]

nets:
  N1: Raspberry_Pi_1.GIPO4, LED1.anode
  N2: Raspberry_Pi_1.GND, Raspberry_Pi_1.GIPO19, LED1.cathode, LED2.cathode, LED3.cathode, LED4.cathode, LED5.cathode, LED6.cathode, LED7.cathode, LED8.cathode, LED9.cathode, LED10.cathode, LED10.anode
  N3: Raspberry_Pi_1.GIPO17, LED2.anode
  N4: Raspberry_Pi_1.GIPO27, LED4.anode
  N5: Raspberry_Pi_1.GIPO22, LED6.anode
  N6: Raspberry_Pi_1.GIPO6, LED9.anode
  N7: Raspberry_Pi_1.GIPO13, LED5.anode
  N8: Raspberry_Pi_1.GIPO24, LED8.anode
  N9: Raspberry_Pi_1.GIPO18, LED3.anode
