# Fritzing sketch 7segment (saved by Fritzing 0.9.3b)

parts:
  부품1 = Arduino Uno (Rev3)
  U1 = 7-SEGMENT-DISPLAY [package=7-segment-display]

nets:
  N1: 부품1.D8, U1.E
  N2: 부품1.D9_PWM, U1.B
  N3: 부품1.D10_PWM/SS, U1.DP
  N4: 부품1.D11_PWM/MOSI, U1.G1
  N5: 부품1.D12/MISO, U1.D
  N6: 부품1.D5_PWM, U1.A
  N7: 부품1.D6_PWM, U1.G2
  N8: 부품1.D7, U1.G
  N9: 부품1.5V, U1.C
