# Fritzing sketch ds18b20 (saved by Fritzing 0.9.3b)
breadboards: 1

parts:
  Raspberry_Pi_1 = Raspberry Pi 3 [part_number=RPI-3-V1.2]
  R1 = Resistor [tolerance=±5% resistance=220 package=THT]
  DS2 = DS18B20 1-Wire Temperature Sensor Probe Cable

nets:
  N1: Raspberry_Pi_1.3v3, R1.Pin_1
  N2: Raspberry_Pi_1.GPIO4, R1.Pin_0, DS2.VDD, DS2.shield
  GND: Raspberry_Pi_1.GND, DS2.GND
